# Fritzing sketch Stargate (saved by Fritzing 0.9.4)

parts:
  R21 = Resistor [tolerance=±5% resistance=56k package=THT]
  Q16 = NPN-Transistor [package="TO92 [THT]"]
  R7 = Resistor [tolerance=±5% resistance=540 package=THT]
  R35 = Resistor [tolerance=±5% resistance=56k package=THT]
  M1 = RioRand LM2596
  R1 = Resistor [tolerance=±5% resistance=540 package=THT]
  Q24 = NPN-Transistor [package="TO92 [THT]"]
  R15 = Resistor [tolerance=±5% resistance=120 package="2512 [SMD]"]
  R36 = Resistor [tolerance=±5% resistance=56k package=THT]
  Q23 = PNP-Transistor [package="TO92 [THT]"]
  R18 = Resistor [tolerance=±5% resistance=10k package=THT]
  J4 = Dagu DGServo 9g header (male) [package=THT]
  R2 = Resistor [tolerance=±5% resistance=540 package=THT]
  Q28 = PNP-Transistor [package="TO92 [THT]"]
  STEPPER = male pin header, 4 pins [form="♂ (male)"]
  C1 = Electrolytic Capacitor [capacitance=100µF package="100 mil [THT, electrolytic]"]
  Q26 = NPN-Transistor [package="TO92 [THT]"]
  Q20 = NPN-Transistor [package="TO92 [THT]"]
  R28 = Resistor [tolerance=±5% resistance=47k package=THT]
  R11 = Resistor [tolerance=±5% resistance=270 package=THT]
  R5 = Resistor [tolerance=±5% resistance=540 package=THT]
  R25 = Resistor [tolerance=±5% resistance=56k package=THT]
  LDR = male pin header, 2 pins [form="♂ (male)"]
  CHEVRONS = male pin header, 10 pins [form="♂ (male)"]
  R26 = Resistor [tolerance=±5% resistance=47k package=THT]
  Q22 = PNP-Transistor [package="TO92 [THT]"]
  Q13 = PNP-Transistor [package="TO92 [THT]"]
  R20 = Resistor [tolerance=±5% resistance=47k package=THT]
  Q27 = PNP-Transistor [package="TO92 [THT]"]
  R24 = Resistor [tolerance=±5% resistance=47k package=THT]
  BUTTONS = male pin header, 3 pins [form="♂ (male)"]
  R27 = Resistor [tolerance=±5% resistance=47k package=THT]
  Q21 = PNP-Transistor [package="TO92 [THT]"]
  R4 = Resistor [tolerance=±5% resistance=540 package=THT]
  Q15 = PNP-Transistor [package="TO92 [THT]"]
  LED = male pin header, 2 pins [form="♂ (male)"]
  Q19 = NPN-Transistor [package="TO92 [THT]"]
  R6 = Resistor [tolerance=±5% resistance=540 package=THT]
  Q17 = PNP-Transistor [package="TO92 [THT]"]
  R31 = Resistor [tolerance=±5% resistance=56k package=THT]
  R9 = Resistor [tolerance=±5% resistance=540 package=THT]
  Q18 = NPN-Transistor [package="TO92 [THT]"]
  R19 = Resistor [tolerance=±5% resistance=1M package=THT]
  R23 = Resistor [tolerance=±5% resistance=56k package=THT]
  R16 = Resistor [tolerance=±5% resistance=10k package=THT]
  R8 = Resistor [tolerance=±5% resistance=540 package=THT]
  Q11 = NPN-Transistor [part_number=BC368 package="TO92 [THT]"]
  RAMP = male pin header, 3 pins [form="♂ (male)"]
  Pololu_A1 = Pololu A4988 [package=SO16]
  R22 = Resistor [tolerance=±5% resistance=47k package=THT]
  Q14 = NPN-Transistor [package="TO92 [THT]"]
  R30 = Resistor [tolerance=±5% resistance=56k package=THT]
  R13 = Resistor [tolerance=±5% resistance=270 package=THT]
  R33 = Resistor [tolerance=±5% resistance=47k package=THT]
  R3 = Resistor [tolerance=±5% resistance=540 package=THT]
  R32 = Resistor [tolerance=±5% resistance=47k package=THT]
  Composant1 = Arduino Nano (Rev3.0)
  R29 = Resistor [tolerance=±5% resistance=56k package=THT]
  Q12 = NPN-Transistor [package="TO92 [THT]"]
  R17 = Resistor [tolerance=±5% resistance=10k package=THT]
  Q29 = PNP-Transistor [package="TO92 [THT]"]
  Q25 = NPN-Transistor [package="TO92 [THT]"]
  R34 = Resistor [tolerance=±5% resistance=47k package=THT]
  R37 = Resistor [tolerance=±5% resistance=56k package=THT]

nets:
  N1: R21.Pin_0, Q13.B, Q12.C
  12V: R21.Pin_1, R35.Pin_1, M1.Pin_1, R36.Pin_1, Q23.E, Q28.E, C1.+, R11.Pin_0, R25.Pin_1, Q22.E, Q13.E, Q27.E, Q21.E, Q15.E, Q17.E, R31.Pin_1, R23.Pin_1, Pololu_A1.VMOT, R30.Pin_1, R13.Pin_0, Composant1.VIN, R29.Pin_1, Q29.E, R37.Pin_1
  GND: Q16.E, M1.Pin_2, M1.Pin_4, Q24.E, R15.Pin_1, R18.Pin_0, C1.-, Q26.E, Q20.E, CHEVRONS.pin10, Q19.E, Q18.E, R19.Pin_0, R16.Pin_1, Q11.E, RAMP.pin2, Pololu_A1.GND, Q14.E, Composant1.GND, Q12.E, Q25.E
  N2: Q16.B, R24.Pin_1
  N3: Q16.C, R25.Pin_0, Q17.B
  N4: R7.Pin_0, Q17.C
  N5: R7.Pin_1, CHEVRONS.pin7
  N6: R35.Pin_0, Q24.C, Q27.B
  5V: M1.Pin_3, J4.Vcc, Pololu_A1.VDD
  N7: R1.Pin_0, Q29.C
  N8: R1.Pin_1, CHEVRONS.pin1
  N9: Q24.B, R32.Pin_1
  N10: R15.Pin_0, LED.pin2
  N11: R36.Pin_0, Q28.B, Q26.C
  N12: Q23.B, Q19.C, R31.Pin_0
  N13: Q23.C, R4.Pin_0
  N14: R18.Pin_1, BUTTONS.pin3, R17.Pin_0
  N15: J4.gnd, Q11.C
  N16: J4.pulse, Composant1.D13/SCK
  N17: R2.Pin_0, Q28.C
  N18: R2.Pin_1, CHEVRONS.pin2
  N19: STEPPER.pin1, Pololu_A1.2B
  N20: STEPPER.pin2, Pololu_A1.2A
  N21: STEPPER.pin3, Pololu_A1.1A
  N22: STEPPER.pin4, Pololu_A1.1B
  N23: Q26.B, R33.Pin_1
  N24: Q20.B, R27.Pin_1
  N25: Q20.C, Q22.B, R30.Pin_0
  N26: R28.Pin_0, Composant1.D7
  N27: R28.Pin_1, Q19.B
  N28: R11.Pin_1, RAMP.pin3
  N29: R5.Pin_0, Q22.C
  N30: R5.Pin_1, CHEVRONS.pin5
  N31: LDR.pin1, BUTTONS.pin1, Composant1.5V, R17.Pin_1
  N32: LDR.pin2, R16.Pin_0, Composant1.A2
  N33: CHEVRONS.pin3, R3.Pin_1
  N34: CHEVRONS.pin4, R4.Pin_1
  N35: CHEVRONS.pin6, R6.Pin_1
  N36: CHEVRONS.pin8, R8.Pin_1
  N37: CHEVRONS.pin9, R9.Pin_1
  N38: R26.Pin_0, Composant1.D5
  N39: R26.Pin_1, Q18.B
  N40: Q13.C, R9.Pin_0
  N41: R20.Pin_0, Composant1.D2
  N42: R20.Pin_1, Q12.B
  N43: Q27.C, R3.Pin_0
  N44: R24.Pin_0, Composant1.D4
  N45: BUTTONS.pin2, R19.Pin_1, Composant1.A1
  N46: R27.Pin_0, Composant1.D6
  N47: Q21.B, Q18.C, R29.Pin_0
  N48: Q21.C, R6.Pin_0
  N49: Q15.B, R23.Pin_0, Q14.C
  N50: Q15.C, R8.Pin_0
  N51: LED.pin1, Composant1.A0
  N52: Q11.B, Composant1.D12/MISO
  N53: RAMP.pin1, R13.Pin_1
  N54: Pololu_A1.ENABLE, Composant1.A5
  N55: Pololu_A1.RESET, Pololu_A1.SLEEP
  N56: Pololu_A1.STEP, Composant1.A4
  N57: Pololu_A1.DIR, Composant1.A3
  N58: R22.Pin_0, Composant1.D3
  N59: R22.Pin_1, Q14.B
  N60: R33.Pin_0, Composant1.D9
  N61: R32.Pin_0, Composant1.D8
  N62: Composant1.D10, R34.Pin_0
  N63: Q29.B, Q25.C, R37.Pin_0
  N64: Q25.B, R34.Pin_1
